# Fritzing sketch Caliper Reader (saved by Fritzing 0.9.3b)
circuit board: 7.88651cm x 4.57482cm
breadboards: 1

parts:
  Q1 = NPN-Transistor [package="TO92 [THT]"]
  R5 = Resistor [tolerance=±5% resistance=10k package=THT]
  R6 = Resistor [tolerance=±5% resistance=10k package=THT]
  Q2 = NPN-Transistor [package="TO92 [THT]"]
  R3 = Resistor [tolerance=±5% resistance=10k package=THT]
  R4 = Resistor [tolerance=±5% resistance=10k package=THT]
  R1 = Resistor [tolerance=±5% resistance=1.5k package=THT]
  R2 = Resistor [tolerance=±5% resistance=680 package=THT]
  ARDUINO_NANO = Arduino Nano (Rev3.0)
  J1 = Camdenboss CTB0158-4 [part_number=CTB0158-4 package=THT]
  R7 = Resistor [tolerance=±5% resistance=1.5k package=THT]  # not connected
  R8 = Resistor [tolerance=±5% resistance=680 package=THT]  # not connected
  R9 = Resistor [tolerance=±5% resistance=10k package=THT]  # not connected
  R10 = Resistor [tolerance=±5% resistance=10k package=THT]  # not connected
  Q3 = NPN-Transistor [package="TO92 [THT]"]  # not connected
  Grove_LCD = Grove OLED 128x96

nets:
  GND: Q1.E, Q2.E, R2.Pin_1, ARDUINO_NANO.GND, J1.pin4, Grove_LCD.GND
  N1: Q1.B, R5.Pin_1
  N2: Q1.C, R6.Pin_0, ARDUINO_NANO.D8
  N3: R5.Pin_0, J1.pin3
  5V: R6.Pin_1, R4.Pin_1, R1.Pin_1, ARDUINO_NANO.5V, Grove_LCD.VCC
  N4: Q2.B, R3.Pin_1
  N5: Q2.C, R4.Pin_0, ARDUINO_NANO.D7
  N6: R3.Pin_0, J1.pin2
  N7: R1.Pin_0, R2.Pin_0, J1.pin1, J1.terminal_1

notes:
  +1,5 VDC
  +5 VDC
  Caliper Reader, (c) 2018 - Nicolò Carandini, 0.1
  1.5kΩ
  680Ω
  10kΩ
  2N2222A
  Seeedstudio Grove LCD
  Caliper Neoteck
